// Logisim project ydriver_amp.circ as structural Verilog: 2 circuits, main circuit driver_amp_tran
module driver_amp_tran (
  input  V4,
  input  V5,
  input  V1,
  input  FR,
  output Driver_VDD,
  output Driver_GND
);

  wire not_1_out, transistor_17_out, transistor_18_out, transistor_19_out, transistor_20_out,
       transistor_21_out, transistor_22_out, transistor_23_out, transistor_24_out;

  Transistor transistor_1 (.in(1'b1), .out(Driver_VDD), .gate(transistor_17_out));
  Transistor transistor_2 (.in(1'b1), .out(Driver_VDD), .gate(transistor_17_out));
  Transistor transistor_3 (.in(1'b1), .out(Driver_VDD), .gate(transistor_17_out));
  Transistor transistor_4 (.in(1'b1), .out(Driver_VDD), .gate(transistor_17_out));
  Transistor transistor_5 (.in(V1), .out(Driver_VDD), .gate(transistor_18_out));
  Transistor transistor_6 (.in(V1), .out(Driver_VDD), .gate(transistor_18_out));
  Transistor transistor_7 (.in(V1), .out(Driver_VDD), .gate(transistor_18_out));
  Transistor transistor_8 (.in(V1), .out(Driver_VDD), .gate(transistor_18_out));
  not not_1 (not_1_out, FR);
  Transistor #(.\type ("n")) transistor_9 (.in(V4), .out(Driver_GND), .gate(transistor_18_out));
  Transistor #(.\type ("n")) transistor_10 (.in(V4), .out(Driver_GND), .gate(transistor_18_out));
  Transistor #(.\type ("n")) transistor_11 (.in(V4), .out(Driver_GND), .gate(transistor_18_out));
  Transistor #(.\type ("n")) transistor_12 (.in(V4), .out(Driver_GND), .gate(transistor_18_out));
  Transistor #(.\type ("n")) transistor_13 (.in(V5), .out(Driver_GND), .gate(transistor_17_out));
  Transistor #(.\type ("n")) transistor_14 (.in(V5), .out(Driver_GND), .gate(transistor_17_out));
  Transistor #(.\type ("n")) transistor_15 (.in(V5), .out(Driver_GND), .gate(transistor_17_out));
  Transistor #(.\type ("n")) transistor_16 (.in(V5), .out(Driver_GND), .gate(transistor_17_out));
  Transistor #(.\type ("n")) transistor_17 (.in(V5), .out(transistor_17_out), .gate(transistor_19_out));
  Transistor #(.\type ("n")) transistor_18 (.in(V5), .out(transistor_18_out), .gate(transistor_20_out));
  Transistor #(.\type ("n")) transistor_19 (.in(V5), .out(transistor_19_out), .gate(transistor_22_out));
  Transistor #(.\type ("n")) transistor_20 (.in(V5), .out(transistor_20_out), .gate(transistor_21_out));
  Transistor #(.\type ("n")) transistor_21 (.in(V5), .out(transistor_21_out), .gate(transistor_23_out));
  Transistor #(.\type ("n")) transistor_22 (.in(V5), .out(transistor_22_out), .gate(transistor_24_out));
  Transistor #(.\type ("n")) transistor_23 (.in(V5), .out(transistor_23_out), .gate(transistor_24_out));
  Transistor #(.\type ("n")) transistor_24 (.in(V5), .out(transistor_24_out), .gate(transistor_23_out));
  Transistor transistor_25 (.in(1'b1), .out(transistor_22_out), .gate(transistor_24_out));
  Transistor transistor_26 (.in(1'b1), .out(transistor_21_out), .gate(transistor_23_out));
  Transistor transistor_27 (.in(1'b1), .out(transistor_19_out), .gate(transistor_22_out));
  Transistor transistor_28 (.in(1'b1), .out(transistor_23_out), .gate(FR));
  Transistor transistor_29 (.in(1'b1), .out(transistor_20_out), .gate(transistor_21_out));
  Transistor transistor_30 (.in(1'b1), .out(transistor_17_out), .gate(transistor_19_out));
  Transistor transistor_31 (.in(1'b1), .out(transistor_17_out), .gate(transistor_19_out));
  Transistor transistor_32 (.in(1'b1), .out(transistor_24_out), .gate(not_1_out));
  Transistor transistor_33 (.in(1'b1), .out(transistor_18_out), .gate(transistor_20_out));
  Transistor transistor_34 (.in(1'b1), .out(transistor_18_out), .gate(transistor_20_out));

  // Notes on the sheet:
  //   VDD
  //   FR = 0
  //   FR = 1
  //   fr_int
  //   n_fr_int
endmodule

module simplified_driver_amp (
  input  FR,
  input  V1,
  input  VDD,
  input  V5,
  input  V4,
  output Driver_VDD,
  output Driver_GND
);

  Multiplexer multiplexer_1 (.in0(V1), .in1(VDD), .out(Driver_VDD), .sel(FR));
  Multiplexer multiplexer_2 (.in0(V5), .in1(V4), .out(Driver_GND), .sel(FR));
endmodule
